# Fritzing sketch circuit (saved by Fritzing 0.9.10b)
perfboards: 2

parts:
  Componente2 = Arduino Pro Mini V2 (5V)
  DFRobot_DFPlayer_Mini1 = DFRobot DFPlayer Mini [part_number=DFR0299]
  S1 = Momentary Switch [package=ksa_sealed_tac_switch]
  J1 = JST XH 2A male [form="♂ (male)" package=THT]
  J2 = JST XH 2A male [form="♂ (male)" package=THT]
  R1 = Resistor [tolerance=±5% resistance=330 package="0805 [SMD]"]  # not connected
  DFRobot_DFPlayer_Mini2 = DFRobot DFPlayer Mini [part_number=DFR0299]
  S2 = Momentary Switch [package=ksa_sealed_tac_switch]
  R2 = Resistor [tolerance=±5% resistance=220 package="0805 [SMD]"]
  Componente3 = Arduino Nano (Rev3.0)
  J3 = JST XH 2A male [form="♂ (male)" package=THT]
  J4 = JST XH 2A male [form="♂ (male)" package=THT]

nets:
  N1: Componente2.RAW, J2.pin2
  VCC: Componente2.VCC, DFRobot_DFPlayer_Mini1.VCC
  N2: Componente2.D4, DFRobot_DFPlayer_Mini1.TX
  N3: Componente2.D3, DFRobot_DFPlayer_Mini1.RX
  N4: Componente2.D2, S1.1
  N5: Componente2.GND, DFRobot_DFPlayer_Mini1.GND-1, DFRobot_DFPlayer_Mini1.GND-2
  N6: DFRobot_DFPlayer_Mini1.SPK_1, J1.pin2
  N7: DFRobot_DFPlayer_Mini1.SPK_2, J1.pin1
  N8: S1.3, J2.pin1
  VCC_2: DFRobot_DFPlayer_Mini2.VCC, Componente3.5V
  N9: DFRobot_DFPlayer_Mini2.RX, Componente3.A5
  N10: DFRobot_DFPlayer_Mini2.TX, Componente3.A4
  N11: DFRobot_DFPlayer_Mini2.SPK_1, J4.pin2
  N12: DFRobot_DFPlayer_Mini2.GND-1, DFRobot_DFPlayer_Mini2.GND-2
  N13: DFRobot_DFPlayer_Mini2.SPK_2, J4.pin1
  N14: S2.1, Componente3.A3
  N15: S2.3, J3.pin1
  N16: S2.4, Componente3.GND
  N17: R2.Pin_1, Componente3.A6
  N18: Componente3.VIN, J3.pin2

custom parts:
  Arduino Pro Mini V2 (5V): Arduino Pro Mini V2 There are several different layouts for this board out there. This one is modeled after the Sparkfun 11113 board but a few of the pins have been moved around.
  JST XH 2A male: JST XH-2A
